# Fritzing sketch PiRangeFinder (saved by Fritzing 0.8.0b)

parts:
  Raspberry_Pi1 = Raspberry Pi
  Part1 = SRF05 Ultrasonic Rangefinder
  R1 = Resistor [tolerance=±5% resistance=1.5k package=THT]
  R2 = Resistor [tolerance=±5% resistance=3.3k package=THT]

nets:
  5V: Raspberry_Pi1.5V, Part1.VCC
  GND: Raspberry_Pi1.GND, Part1.GND, R1.Pin_1
  N1: Raspberry_Pi1.GPIO4, Part1.Trig
  N2: Raspberry_Pi1.GPIO5, R1.Pin_0, R2.Pin_0
  N3: Part1.Echo, R2.Pin_1
